// Logisim project 3er_lab.circ as structural Verilog
module main (
);

  IFetch ifetch_1 ();  // open: PCNext, CLK, Reset, PCPlus4, Instruction
  IBreackDown ibreackdown_1 ();  // open: Instruction, Funct, Shamt, RD, RT, RS, OPCode, Inmediate, Address
  RegFile regfile_1 ();  // open: ReadReg1, ReadReg2, RegWrite, WriteReg, WriteData, CLK, Reset, ReadData1, ReadData2
  ALU alu_1 ();  // open: In1, In2, ALUOperation, Result, Zero
endmodule

module IFetch (
  input  [31:0] PCNext,
  input  CLK,
  input  Reset,
  output [31:0] PCPlus4,
  output [31:0] Instruction
);

  wire [31:0] PCReg_q;

  Register #(.width(32)) PCReg (.D(PCNext), .clk(CLK), .Q(PCReg_q), .clr(Reset));  // open: en
  // Probe on PCReg_q
  // Probe on PCReg_q[25:2]
  ROM #(.addrWidth(24), .dataWidth(32)) rom_1 (.addr(PCReg_q[25:2]), .data(Instruction));
  Adder #(.width(32)) adder_1 (.a(PCReg_q), .b(32'h4), .out(PCPlus4));  // open: cin, cout

  // Notes on the sheet:
  //   contents of rom_1 (hex, n*v repeats v):
  //   8c080002 8c090004 1095020
endmodule

module RegFile (
  input  [4:0] ReadReg1,
  input  [4:0] ReadReg2,
  input  RegWrite,
  input  [4:0] WriteReg,
  input  [31:0] WriteData,
  input  CLK,
  input  Reset,
  output [31:0] ReadData1,
  output [31:0] ReadData2
);

  wire W0, W1, W2, W3, W4, W5, W6, W7, W8, W9, W10, W11, W12, W13, W14, W15, W16, W17, W18, W19, W20, W21,
       W22, W23, W24, W25, W26, W27, W28, W29, W30, W31;
  wire [31:0] R0, R1, R2, R3, R4, R5, R6, R7, R8, R9, R10, R11, R12, R13, R14, R15, R16, R17, R18, R19, R20,
       R21, R22, R23, R24, R25, R26, R27, R28, R29, R30, R31;

  Decoder #(.select(5)) decoder_1 (
    .out0(W0), .out1(W1), .out2(W2), .out3(W3), .out4(W4), .out5(W5), .out6(W6), .out7(W7), .out8(W8),
    .out9(W9), .out10(W10), .out11(W11), .out12(W12), .out13(W13), .out14(W14), .out15(W15), .out16(W16),
    .out17(W17), .out18(W18), .out19(W19), .out20(W20), .out21(W21), .out22(W22), .out23(W23), .out24(W24),
    .out25(W25), .out26(W26), .out27(W27), .out28(W28), .out29(W29), .out30(W30), .out31(W31),
    .sel(WriteReg), .en(RegWrite));
  Register #(.width(32)) zero (.D({32{1'b0}}), .en(W0), .clk(CLK), .Q(R0), .clr(Reset));
  Register #(.width(32)) at (.D(WriteData), .en(W1), .clk(CLK), .Q(R1), .clr(Reset));
  Register #(.width(32)) v0 (.D(WriteData), .en(W2), .clk(CLK), .Q(R2), .clr(Reset));
  Register #(.width(32)) v1 (.D(WriteData), .en(W3), .clk(CLK), .Q(R3), .clr(Reset));
  Register #(.width(32)) a0 (.D(WriteData), .en(W4), .clk(CLK), .Q(R4), .clr(Reset));
  Register #(.width(32)) a1 (.D(WriteData), .en(W5), .clk(CLK), .Q(R5), .clr(Reset));
  Register #(.width(32)) a2 (.D(WriteData), .en(W6), .clk(CLK), .Q(R6), .clr(Reset));
  Register #(.width(32)) a3 (.D(WriteData), .en(W7), .clk(CLK), .Q(R7), .clr(Reset));
  Multiplexer #(.select(5), .width(32)) multiplexer_1 (
    .in0(R0), .in1(R1), .in2(R2), .in3(R3), .in4(R4), .in5(R5), .in6(R6), .in7(R7), .in8(R8), .in9(R9),
    .in10(R10), .in11(R11), .in12(R12), .in13(R13), .in14(R14), .in15(R15), .in16(R16), .in17(R17),
    .in18(R18), .in19(R19), .in20(R20), .in21(R21), .in22(R22), .in23(R23), .in24(R24), .in25(R25),
    .in26(R26), .in27(R27), .in28(R28), .in29(R29), .in30(R30), .in31(R31), .out(ReadData1), .sel(ReadReg1));
  Register #(.width(32)) t0 (.D(WriteData), .en(W8), .clk(CLK), .Q(R8), .clr(Reset));
  Register #(.width(32)) t1 (.D(WriteData), .en(W9), .clk(CLK), .Q(R9), .clr(Reset));
  Register #(.width(32)) t2 (.D(WriteData), .en(W10), .clk(CLK), .Q(R10), .clr(Reset));
  Register #(.width(32)) t3 (.D(WriteData), .en(W11), .clk(CLK), .Q(R11), .clr(Reset));
  Register #(.width(32)) t4 (.D(WriteData), .en(W12), .clk(CLK), .Q(R12), .clr(Reset));
  Register #(.width(32)) t5 (.D(WriteData), .en(W13), .clk(CLK), .Q(R13), .clr(Reset));
  Register #(.width(32)) t6 (.D(WriteData), .en(W14), .clk(CLK), .Q(R14), .clr(Reset));
  Register #(.width(32)) t7 (.D(WriteData), .en(W15), .clk(CLK), .Q(R15), .clr(Reset));
  Multiplexer #(.select(5), .width(32)) multiplexer_2 (
    .in0(R0), .in1(R1), .in2(R2), .in3(R3), .in4(R4), .in5(R5), .in6(R6), .in7(R7), .in8(R8), .in9(R9),
    .in10(R10), .in11(R11), .in12(R12), .in13(R13), .in14(R14), .in15(R15), .in16(R16), .in17(R17),
    .in18(R18), .in19(R19), .in20(R20), .in21(R21), .in22(R22), .in23(R23), .in24(R24), .in25(R25),
    .in26(R26), .in27(R27), .in28(R28), .in29(R29), .in30(R30), .in31(R31), .out(ReadData2), .sel(ReadReg2));
  Register #(.width(32)) s0 (.D(WriteData), .en(W16), .clk(CLK), .Q(R16), .clr(Reset));
  Register #(.width(32)) s1 (.D(WriteData), .en(W17), .clk(CLK), .Q(R17), .clr(Reset));
  Register #(.width(32)) s2 (.D(WriteData), .en(W18), .clk(CLK), .Q(R18), .clr(Reset));
  Register #(.width(32)) s3 (.D(WriteData), .en(W19), .clk(CLK), .Q(R19), .clr(Reset));
  Register #(.width(32)) s4 (.D(WriteData), .en(W20), .clk(CLK), .Q(R20), .clr(Reset));
  Register #(.width(32)) s5 (.D(WriteData), .en(W21), .clk(CLK), .Q(R21), .clr(Reset));
  Register #(.width(32)) s6 (.D(WriteData), .en(W22), .clk(CLK), .Q(R22), .clr(Reset));
  Register #(.width(32)) s7 (.D(WriteData), .en(W23), .clk(CLK), .Q(R23), .clr(Reset));
  Register #(.width(32)) t8 (.D(WriteData), .en(W24), .clk(CLK), .Q(R24), .clr(Reset));
  Register #(.width(32)) t9 (.D(WriteData), .en(W25), .clk(CLK), .Q(R25), .clr(Reset));
  Register #(.width(32)) k0 (.D(WriteData), .en(W26), .clk(CLK), .Q(R26), .clr(Reset));
  Register #(.width(32)) k1 (.D(WriteData), .en(W27), .clk(CLK), .Q(R27), .clr(Reset));
  Register #(.width(32)) gp (.D(WriteData), .en(W28), .clk(CLK), .Q(R28), .clr(Reset));
  Register #(.width(32)) sp (.D(WriteData), .en(W29), .clk(CLK), .Q(R29), .clr(Reset));
  Register #(.width(32)) fp (.D(WriteData), .en(W30), .clk(CLK), .Q(R30), .clr(Reset));
  Register #(.width(32)) ra (.D(WriteData), .en(W31), .clk(CLK), .Q(R31), .clr(Reset));

  // Other names for the same wires on the sheet: RD1[31:0] = ReadData1; RD2[31:0] = ReadData2; RR1[4:0] = ReadReg1;
  //   RR2[4:0] = ReadReg2; RW = RegWrite; WR[4:0] = WriteReg
endmodule

module ALU (
  input  [31:0] In1,
  input  [31:0] In2,
  input  [2:0] ALUOperation,
  output [31:0] Result,
  output Zero
);

  wire [0:0] OP2;
  wire [31:0] OP0, OP1, OP4, OP5, OP6, undriven, undriven_2;

  Subtractor #(.width(32)) subtractor_1 (.a(In1), .b(In2), .out(OP0));  // open: bin, bout
  Adder #(.width(32)) adder_1 (.a(In1), .b(In2), .out(OP1));  // open: cin, cout
  Comparator #(.width(32)) comparator_1 (.a(In1), .b(In2), .lt(OP2[0]));  // open: gt, eq
  assign OP4 = In1 & In2;  // AND_Gate and_1, 32 bits wide
  assign OP5 = ~(In1 | In2);  // NOR_Gate nor_1, 32 bits wide
  assign OP6 = In1 | In2;  // OR_Gate or_1, 32 bits wide
  Multiplexer #(.select(3), .width(32)) multiplexer_1 (
    .in0(OP0), .in1(OP1), .in2({{31{1'b0}}, OP2[0]}), .in3(undriven), .in4(OP4), .in5(OP4), .in6(OP4),
    .in7(undriven_2), .out(Result), .sel(ALUOperation));
  // Probe on Result

  assign Zero = 1'b0;

  // Other names for the same wires on the sheet: ALUOp[2:0] = ALUOperation

  // Notes on the sheet:
  //   011 -> 
  //   111 -> 
  //   000 -> SUB
  //   001 -> ADD
  //   010 -> SLT
  //   100 -> AND
  //   101 -> NOR
  //   110 -> OR
endmodule

module IBreackDown (
  input  [31:0] Instruction,
  output [5:0] Funct,
  output [4:0] Shamt,
  output [4:0] RD,
  output [4:0] RT,
  output [4:0] RS,
  output [5:0] OPCode,
  output [15:0] Inmediate,
  output [25:0] Address
);


  assign Address = Instruction[25:0];
  assign Funct = Instruction[5:0];
  assign Inmediate = Instruction[15:0];
  assign OPCode = Instruction[31:26];
  assign RD = Instruction[15:11];
  assign RS = Instruction[25:21];
  assign RT = Instruction[20:16];
  assign Shamt = Instruction[10:6];

  // Other names for the same wires on the sheet: ADDR[25:0] = Instruction[25:0]; INM[15:0] = Instruction[15:0]

  // Notes on the sheet:
  //   10 - 6
  //   15-11
  //   20-16
  //   25-21
  //   26-31
endmodule

module DataMemory (
  input  [31:0] Address,
  input  [31:0] WriteData,
  input  MemWrite,
  input  MemRead,
  input  CLK,
  output [31:0] ReadData
);

  wire [7:0] multiplexer_1_out;
  wire [31:0] ram_1_dout;

  RAM #(.addrWidth(24), .dataWidth(32)) ram_1 (
    .addr(Address[25:2]), .we(MemWrite), .oe(MemRead), .clk(CLK), .din(WriteData), .dout(ram_1_dout));
  Multiplexer #(.select(2), .width(8)) multiplexer_1 (
    .in0(ram_1_dout[7:0]), .in1(ram_1_dout[15:8]), .in2(ram_1_dout[23:16]), .in3(ram_1_dout[31:24]),
    .out(multiplexer_1_out), .sel(Address[1:0]));
  // Probe on Address[1:0]
  assign ReadData = {{24{multiplexer_1_out[7]}}, multiplexer_1_out};  // Bit_Extender bit_extender_1
endmodule
