// Logisim project 3er_lab_v3.circ as structural Verilog: 8 circuits, main circuit main
module main (
  input  in_1
);

  wire ALUSRC, and_1_out, BRANCH, CLK, JR_ENABLE, JUMP, JUMPREG, MEMREAD, MEMWRITE, or_1_out, REGWRITE, ZERO;
  wire [1:0] ALUOP, LOADTYPE, MEMTOREG, REGDST;
  wire [2:0] ALUOpControl;
  wire [4:0] bit_extender_2_out, multiplexer_3_out, RD, RS, RT, SHAMT;
  wire [5:0] FUNCT, multiplexer_6_out, OPCODE;
  wire [15:0] INMEDIATE;
  wire [25:0] ADDRESS, shifter_1_out;
  wire [27:0] PCPLUS4;
  wire [31:0] adder_1_out, ALURESULT, bit_extender_3_out, datamemory_1_readdata, DATAWRITER,
       ifetch_1_instruction, INMED32B, JUMPADDR, multiplexer_1_out, multiplexer_2_out, multiplexer_4_out,
       multiplexer_7_out, PCNEXT, READDATA1, READDATA2, shifter_2_out, shifter_3_out, shifter_4_out;

  // Probe on ADDRESS
  Clock clock_1 (.out(CLK));
  // Probe on PCNEXT
  assign JUMPADDR[27:0] = {{2{shifter_1_out[25]}}, shifter_1_out};  // Bit_Extender bit_extender_1
  Shifter #(.width(26)) shifter_1 (.in(ADDRESS), .\dist (5'b00010), .out(shifter_1_out));
  // Probe on {JUMPADDR[31:28], PCPLUS4}
  IFetch ifetch_1 (
    .PCNext(PCNEXT), .CLK(CLK), .Reset(in_1), .PCPlus4({JUMPADDR[31:28], PCPLUS4}),
    .Instruction(ifetch_1_instruction));
  // Probe on JUMPADDR[27:0]
  // Probe on JUMPADDR[31:28]
  // Probe on {JUMPADDR[31:28], PCPLUS4}
  // Probe on JUMPADDR
  // Probe on INMED32B
  IBreakDown ibreakdown_1 (
    .Instruction(ifetch_1_instruction), .Funct(FUNCT), .Shamt(SHAMT), .RD(RD), .RT(RT), .RS(RS),
    .OPCode(OPCODE), .Inmediate(INMEDIATE), .Address(ADDRESS));
  // Probe on shifter_2_out
  Shifter #(.width(32)) shifter_2 (.in(INMED32B), .\dist (5'b00010), .out(shifter_2_out));
  // Probe on ADDRESS
  assign bit_extender_2_out = {{4{OPCODE[5]}}, OPCODE[5]};  // Bit_Extender bit_extender_2
  // Probe on {JUMPADDR[31:28], PCPLUS4}
  Adder #(.width(32)) adder_1 (
    .a({JUMPADDR[31:28], PCPLUS4}), .b(shifter_2_out), .out(adder_1_out));  // open: cin, cout
  // Probe on REGDST
  Multiplexer #(.width(32)) multiplexer_1 (
    .in0({JUMPADDR[31:28], PCPLUS4}), .in1(adder_1_out), .out(multiplexer_1_out), .sel(and_1_out));
  Multiplexer #(.width(32)) multiplexer_2 (.in1(INMED32B), .out(multiplexer_2_out), .sel(and_1_out));  // open: in0
  and and_1 (and_1_out, BRANCH, ZERO);
  // Probe on multiplexer_3_out
  Multiplexer #(.select(2), .width(5)) multiplexer_3 (
    .in0(RT), .in1(RD), .in2({5{1'b1}}), .out(multiplexer_3_out), .sel(REGDST));  // open: in3
  assign bit_extender_3_out = {{20{1'b0}}, JUMPADDR[11:0]};  // Bit_Extender bit_extender_3
  // Probe on bit_extender_3_out
  Multiplexer #(.width(32)) multiplexer_4 (
    .in0(multiplexer_1_out), .in1(bit_extender_3_out), .out(multiplexer_4_out), .sel(JUMP));
  // Probe on READDATA1
  RegFile regfile_1 (
    .ReadReg1(RS), .ReadReg2(RT), .RegWrite(REGWRITE), .WriteReg(multiplexer_3_out), .WriteData(DATAWRITER),
    .CLK(CLK), .Reset(in_1), .ReadData1(READDATA1), .ReadData2(READDATA2));
  assign INMED32B = {{16{INMEDIATE[15]}}, INMEDIATE};  // Bit_Extender bit_extender_4
  Control control_1 (
    .OpCode(OPCODE), .RegDst(REGDST), .ALUSrc(ALUSRC), .MemToReg(MEMTOREG), .RegWrite(REGWRITE),
    .MemRead(MEMREAD), .MemWrite(MEMWRITE), .Branch(BRANCH), .Jump(JUMP), .JumpReg(JUMPREG), .ALUOp(ALUOP),
    .LoadType(LOADTYPE));
  // Probe on ALUOP
  // Probe on READDATA2
  Shifter #(.width(32)) shifter_3 (.in(READDATA1), .\dist (5'b00010), .out(shifter_3_out));
  // Probe on PCNEXT
  Multiplexer #(.width(32)) multiplexer_5 (.in0(multiplexer_4_out), .in1(shifter_3_out), .out(PCNEXT), .sel(JR_ENABLE));
  // Probe on ALUOP
  // Probe on READDATA2
  // Probe on INMED32B
  Multiplexer #(.width(6)) multiplexer_6 (.in0(FUNCT), .in1(OPCODE), .out(multiplexer_6_out), .sel(or_1_out));
  or or_1 (or_1_out, ALUSRC, BRANCH);
  Multiplexer #(.width(32)) multiplexer_7 (.in0(READDATA2), .in1(INMED32B), .out(multiplexer_7_out), .sel(ALUSRC));
  ALUControl alucontrol_1 (.ALUOp(ALUOP), .Funct(multiplexer_6_out), .Operation(ALUOpControl), .Jr(JR_ENABLE));
  // Probe on ZERO
  ALU alu_1 (
    .In1(READDATA1), .In2(multiplexer_7_out), .ALUOperation(ALUOpControl), .Shamt(SHAMT), .Zero(ZERO),
    .Result(ALURESULT));
  // Probe on ALURESULT
  // Probe on {JUMPADDR[31:28], PCPLUS4}
  DataMemory datamemory_1 (
    .Address(ALURESULT), .WriteData(READDATA2), .MemWrite(MEMWRITE), .MemRead(MEMREAD), .CLK(CLK),
    .LoadType(LOADTYPE), .ReadData(datamemory_1_readdata));
  Shifter #(.shift("lr"), .width(32)) shifter_4 (
    .in({JUMPADDR[31:28], PCPLUS4}), .\dist (5'b00010), .out(shifter_4_out));
  Multiplexer #(.select(2), .width(32)) multiplexer_8 (
    .in0(ALURESULT), .in1(datamemory_1_readdata), .in2(shifter_4_out), .out(DATAWRITER), .sel(MEMTOREG));  // open: in3
  // Probe on shifter_4_out
  // Probe on DATAWRITER
  // Probe on MEMTOREG

  // Other names for the same wires on the sheet: PCPLUS4[31:28] = JUMPADDR[31:28]; RESET = in_1
endmodule

module IFetch (
  input  [31:0] PCNext,
  input  CLK,
  input  Reset,
  output [31:0] PCPlus4,
  output [31:0] Instruction
);

  wire [31:0] PCReg_q, shifter_1_out;

  Register #(.width(32)) PCReg (.D(PCNext), .clk(CLK), .Q(PCReg_q), .clr(Reset));  // open: en
  // Probe on PCReg_q
  // Probe on PCReg_q
  // Probe on shifter_1_out
  Shifter #(.shift("lr"), .width(32)) shifter_1 (.in(PCReg_q), .\dist (5'b00010), .out(shifter_1_out));
  // Probe on PCReg_q[25:2]
  ROM #(.addrWidth(24), .dataWidth(32)) rom_1 (.addr(PCReg_q[25:2]), .data(Instruction));
  Adder #(.width(32)) adder_1 (.a(PCReg_q), .b(32'h4), .out(PCPlus4));  // open: cin, cout

  // Notes on the sheet:
  //   contents of rom_1 (hex, n*v repeats v):
  //   20080023 ac080000 20080005 ac080004 2008004e ac080008 2008ffe2 ac08000c 2008ffc7 ac080010 20080053
  //   ac080014 2008ffdb ac080018 20080060 ac08001c 2008ffb4 ac080020 2008ffa3 ac080024 2008ffaa ac080028
  //   2008ffc0 ac08002c 2008ffd2 ac080030 20080053 ac080034 20080011 ac080038 2008002f ac08003c 2010000f
  //   8820 9020 230082a 10200014 211a022 9020 254082a 10200009 122080 8c880000 20850004 8ca90000 109082a
  //   10200001 c000034 22520001 8000027 22310001 8000023 8c880000 8ca90000 ac890000 aca80000 3e00008 b020
  //   4020 20090000 110082a 10200008 8d240000 308a0001 11400003 21080001 21290004 800003c 22d60001 8000041
  //   22100001 216a822
endmodule

module RegFile (
  input  [4:0] ReadReg1,
  input  [4:0] ReadReg2,
  input  RegWrite,
  input  [4:0] WriteReg,
  input  [31:0] WriteData,
  input  CLK,
  input  Reset,
  output [31:0] ReadData1,
  output [31:0] ReadData2
);

  wire W0, W1, W2, W3, W4, W5, W6, W7, W8, W9, W10, W11, W12, W13, W14, W15, W16, W17, W18, W19, W20, W21,
       W22, W23, W24, W25, W26, W27, W28, W29, W30, W31;
  wire [31:0] R0, R1, R2, R3, R4, R5, R6, R7, R8, R9, R10, R11, R12, R13, R14, R15, R16, R17, R18, R19, R20,
       R21, R22, R23, R24, R25, R26, R27, R28, R29, R30, R31;

  Decoder #(.select(5)) decoder_1 (
    .out0(W0), .out1(W1), .out2(W2), .out3(W3), .out4(W4), .out5(W5), .out6(W6), .out7(W7), .out8(W8),
    .out9(W9), .out10(W10), .out11(W11), .out12(W12), .out13(W13), .out14(W14), .out15(W15), .out16(W16),
    .out17(W17), .out18(W18), .out19(W19), .out20(W20), .out21(W21), .out22(W22), .out23(W23), .out24(W24),
    .out25(W25), .out26(W26), .out27(W27), .out28(W28), .out29(W29), .out30(W30), .out31(W31),
    .sel(WriteReg), .en(RegWrite));
  Register #(.width(32)) zero (.D({32{1'b0}}), .en(W0), .clk(CLK), .Q(R0), .clr(Reset));
  Register #(.width(32)) at (.D(WriteData), .en(W1), .clk(CLK), .Q(R1), .clr(Reset));
  Register #(.width(32)) v0 (.D(WriteData), .en(W2), .clk(CLK), .Q(R2), .clr(Reset));
  Register #(.width(32)) v1 (.D(WriteData), .en(W3), .clk(CLK), .Q(R3), .clr(Reset));
  Register #(.width(32)) a0 (.D(WriteData), .en(W4), .clk(CLK), .Q(R4), .clr(Reset));
  Register #(.width(32)) a1 (.D(WriteData), .en(W5), .clk(CLK), .Q(R5), .clr(Reset));
  Register #(.width(32)) a2 (.D(WriteData), .en(W6), .clk(CLK), .Q(R6), .clr(Reset));
  Register #(.width(32)) a3 (.D(WriteData), .en(W7), .clk(CLK), .Q(R7), .clr(Reset));
  Multiplexer #(.select(5), .width(32)) multiplexer_1 (
    .in0(R0), .in1(R1), .in2(R2), .in3(R3), .in4(R4), .in5(R5), .in6(R6), .in7(R7), .in8(R8), .in9(R9),
    .in10(R10), .in11(R11), .in12(R12), .in13(R13), .in14(R14), .in15(R15), .in16(R16), .in17(R17),
    .in18(R18), .in19(R19), .in20(R20), .in21(R21), .in22(R22), .in23(R23), .in24(R24), .in25(R25),
    .in26(R26), .in27(R27), .in28(R28), .in29(R29), .in30(R30), .in31(R31), .out(ReadData1), .sel(ReadReg1));
  Register #(.width(32)) t0 (.D(WriteData), .en(W8), .clk(CLK), .Q(R8), .clr(Reset));
  Register #(.width(32)) t1 (.D(WriteData), .en(W9), .clk(CLK), .Q(R9), .clr(Reset));
  Register #(.width(32)) t2 (.D(WriteData), .en(W10), .clk(CLK), .Q(R10), .clr(Reset));
  Register #(.width(32)) t3 (.D(WriteData), .en(W11), .clk(CLK), .Q(R11), .clr(Reset));
  Register #(.width(32)) t4 (.D(WriteData), .en(W12), .clk(CLK), .Q(R12), .clr(Reset));
  Register #(.width(32)) t5 (.D(WriteData), .en(W13), .clk(CLK), .Q(R13), .clr(Reset));
  Register #(.width(32)) t6 (.D(WriteData), .en(W14), .clk(CLK), .Q(R14), .clr(Reset));
  Register #(.width(32)) t7 (.D(WriteData), .en(W15), .clk(CLK), .Q(R15), .clr(Reset));
  Multiplexer #(.select(5), .width(32)) multiplexer_2 (
    .in0(R0), .in1(R1), .in2(R2), .in3(R3), .in4(R4), .in5(R5), .in6(R6), .in7(R7), .in8(R8), .in9(R9),
    .in10(R10), .in11(R11), .in12(R12), .in13(R13), .in14(R14), .in15(R15), .in16(R16), .in17(R17),
    .in18(R18), .in19(R19), .in20(R20), .in21(R21), .in22(R22), .in23(R23), .in24(R24), .in25(R25),
    .in26(R26), .in27(R27), .in28(R28), .in29(R29), .in30(R30), .in31(R31), .out(ReadData2), .sel(ReadReg2));
  Register #(.width(32)) s0 (.D(WriteData), .en(W16), .clk(CLK), .Q(R16), .clr(Reset));
  Register #(.width(32)) s1 (.D(WriteData), .en(W17), .clk(CLK), .Q(R17), .clr(Reset));
  Register #(.width(32)) s2 (.D(WriteData), .en(W18), .clk(CLK), .Q(R18), .clr(Reset));
  Register #(.width(32)) s3 (.D(WriteData), .en(W19), .clk(CLK), .Q(R19), .clr(Reset));
  Register #(.width(32)) s4 (.D(WriteData), .en(W20), .clk(CLK), .Q(R20), .clr(Reset));
  Register #(.width(32)) s5 (.D(WriteData), .en(W21), .clk(CLK), .Q(R21), .clr(Reset));
  Register #(.width(32)) s6 (.D(WriteData), .en(W22), .clk(CLK), .Q(R22), .clr(Reset));
  Register #(.width(32)) s7 (.D(WriteData), .en(W23), .clk(CLK), .Q(R23), .clr(Reset));
  Register #(.width(32)) t8 (.D(WriteData), .en(W24), .clk(CLK), .Q(R24), .clr(Reset));
  Register #(.width(32)) t9 (.D(WriteData), .en(W25), .clk(CLK), .Q(R25), .clr(Reset));
  Register #(.width(32)) k0 (.D(WriteData), .en(W26), .clk(CLK), .Q(R26), .clr(Reset));
  Register #(.width(32)) k1 (.D(WriteData), .en(W27), .clk(CLK), .Q(R27), .clr(Reset));
  Register #(.width(32)) gp (.D(WriteData), .en(W28), .clk(CLK), .Q(R28), .clr(Reset));
  Register #(.width(32)) sp (.D(WriteData), .en(W29), .clk(CLK), .Q(R29), .clr(Reset));
  Register #(.width(32)) fp (.D(WriteData), .en(W30), .clk(CLK), .Q(R30), .clr(Reset));
  Register #(.width(32)) ra (.D(WriteData), .en(W31), .clk(CLK), .Q(R31), .clr(Reset));

  // Other names for the same wires on the sheet: RD1[31:0] = ReadData1; RD2[31:0] = ReadData2; RR1[4:0] = ReadReg1;
  //   RR2[4:0] = ReadReg2; RW = RegWrite; WR[4:0] = WriteReg
endmodule

module ALU (
  input  [31:0] In1,
  input  [31:0] In2,
  input  [2:0] ALUOperation,
  input  [4:0] Shamt,
  output Zero,
  output [31:0] Result
);

  wire [0:0] OP2;
  wire [31:0] OP0, OP1, OP4, OP5, OP6, OP7, undriven;

  Subtractor #(.width(32)) subtractor_1 (.a(In1), .b(In2), .out(OP0));  // open: bin, bout
  Adder #(.width(32)) adder_1 (.a(In1), .b(In2), .out(OP1));  // open: cin, cout
  Comparator #(.width(32)) comparator_1 (.a(In1), .b(In2), .lt(OP2[0]));  // open: gt, eq
  assign OP4 = In1 & In2;  // AND_Gate and_1, 32 bits wide
  assign OP5 = ~(In1 | In2);  // NOR_Gate nor_1, 32 bits wide
  assign OP6 = In1 | In2;  // OR_Gate or_1, 32 bits wide
  Shifter #(.width(32)) shifter_1 (.in(In2), .\dist (Shamt), .out(OP7));
  Multiplexer #(.select(3), .width(32)) multiplexer_1 (
    .in0(OP0), .in1(OP1), .in2({{31{1'b0}}, OP2[0]}), .in3(OP7), .in4(OP4), .in5(OP5), .in6(OP6),
    .in7(undriven), .out(Result), .sel(ALUOperation));
  // Probe on Result
  Comparator #(.width(32)) comparator_2 (.a(Result), .b({32{1'b0}}), .eq(Zero));  // open: gt, lt

  // Other names for the same wires on the sheet: ALUOp[2:0] = ALUOperation

  // Notes on the sheet:
  //   111 -> 
  //   000 -> SUB
  //   001 -> ADD
  //   010 -> SLT
  //   011 -> sll 
  //   100 -> AND
  //   101 -> NOR
  //   110 -> OR
endmodule

module Control (
  input  [5:0] OpCode,
  output [1:0] RegDst,
  output ALUSrc,
  output [1:0] MemToReg,
  output RegWrite,
  output MemRead,
  output MemWrite,
  output Branch,
  output Jump,
  output JumpReg,
  output [1:0] ALUOp,
  output [1:0] LoadType
);

  wire and_2_out, and_3_out, and_4_out, and_5_out, and_7_out, and_8_out, and_9_out, and_12_out, and_13_out,
       and_14_out, and_15_out, and_18_out, and_19_out, and_20_out, and_21_out, not_1_out, not_2_out,
       not_3_out, not_4_out, not_5_out, not_6_out;

  not not_1 (not_1_out, OpCode[5]);
  not not_2 (not_2_out, OpCode[4]);
  not not_3 (not_3_out, OpCode[3]);
  not not_4 (not_4_out, OpCode[2]);
  not not_5 (not_5_out, OpCode[1]);
  not not_6 (not_6_out, OpCode[0]);
  and and_1 (RegDst[1], not_1_out, OpCode[0]);
  and and_2 (and_2_out, not_3_out, not_4_out, not_5_out);
  and and_3 (and_3_out, not_3_out, not_5_out, not_6_out);
  and and_4 (and_4_out, not_1_out, not_3_out, not_5_out);
  and and_5 (and_5_out, OpCode[4], not_3_out, not_5_out);
  or or_1 (ALUSrc, OpCode[0], OpCode[3]);
  and and_6 (MemToReg[1], not_1_out, OpCode[0]);
  and and_7 (and_7_out, not_4_out, not_5_out);
  and and_8 (and_8_out, not_3_out, OpCode[0]);
  and and_9 (and_9_out, OpCode[3], not_5_out);
  and and_10 (MemRead, OpCode[5], not_3_out);
  and and_11 (MemWrite, OpCode[3], OpCode[1]);
  and and_12 (and_12_out, not_3_out, OpCode[2], not_6_out);
  and and_13 (and_13_out, not_1_out, not_3_out, OpCode[2]);
  and and_14 (and_14_out, not_3_out, OpCode[2], OpCode[1]);
  and and_15 (and_15_out, OpCode[4], not_3_out, OpCode[2]);
  and and_16 (Jump, not_1_out, OpCode[1]);
  and and_17 (ALUOp[1], not_3_out, not_4_out, not_5_out);
  and and_18 (and_18_out, not_3_out, OpCode[2], not_6_out);
  and and_19 (and_19_out, not_1_out, not_3_out, OpCode[2]);
  and and_20 (and_20_out, not_3_out, OpCode[2], OpCode[1]);
  and and_21 (and_21_out, OpCode[4], not_3_out, OpCode[2]);
  and and_22 (LoadType[0], OpCode[5], not_2_out, not_3_out, OpCode[2], not_5_out, OpCode[0]);
  or or_2 (RegDst[0], and_2_out, and_3_out, and_4_out, and_5_out);
  or or_3 (RegWrite, and_7_out, and_8_out, and_9_out);
  or or_4 (Branch, and_12_out, and_13_out, and_14_out, and_15_out);
  or or_5 (ALUOp[0], and_18_out, and_19_out, and_20_out, and_21_out);

  assign JumpReg = 1'b0;
  assign LoadType[1] = 1'b0;
  assign MemToReg[0] = OpCode[5];
endmodule

module ALUControl (
  input  [1:0] ALUOp,
  input  [5:0] Funct,
  output [2:0] Operation,
  output Jr
);

  wire and_1_out, and_2_out, and_3_out, and_4_out, and_5_out, and_6_out, and_7_out, and_8_out, and_9_out,
       and_10_out, and_11_out, and_12_out, and_13_out, and_14_out, and_15_out, and_16_out, and_17_out,
       and_18_out, and_19_out, not_1_out, not_2_out, not_3_out, not_4_out, not_5_out, not_6_out, not_7_out,
       not_8_out;

  not not_1 (not_1_out, ALUOp[1]);
  not not_2 (not_2_out, ALUOp[0]);
  not not_3 (not_3_out, Funct[5]);
  not not_4 (not_4_out, Funct[4]);
  not not_5 (not_5_out, Funct[3]);
  not not_6 (not_6_out, Funct[2]);
  not not_7 (not_7_out, Funct[1]);
  not not_8 (not_8_out, Funct[0]);
  and and_1 (and_1_out, Funct[2], Funct[0]);
  and and_2 (and_2_out, Funct[2], Funct[1]);
  and and_3 (and_3_out, Funct[3], Funct[2]);
  and and_4 (and_4_out, Funct[4], Funct[2]);
  and and_5 (and_5_out, Funct[5], Funct[2]);
  and and_6 (and_6_out, ALUOp[1], Funct[2]);
  and and_7 (and_7_out, not_3_out, not_5_out, not_6_out);
  and and_8 (and_8_out, not_3_out, Funct[1]);
  and and_9 (and_9_out, not_3_out, Funct[4]);
  and and_10 (and_10_out, not_7_out, Funct[0]);
  and and_11 (and_11_out, Funct[4], Funct[3]);
  and and_12 (and_12_out, ALUOp[0], Funct[3]);
  and and_13 (and_13_out, ALUOp[1], not_3_out);
  and and_14 (and_14_out, ALUOp[1], Funct[3]);
  and and_15 (and_15_out, Funct[5], Funct[3], not_8_out);
  and and_16 (and_16_out, Funct[5], Funct[3], Funct[2]);
  and and_17 (and_17_out, not_1_out, not_2_out, not_3_out, not_4_out, not_5_out, not_7_out, not_8_out);
  and and_18 (and_18_out, Funct[1], Funct[0]);
  and and_19 (and_19_out, not_6_out, not_7_out);
  and and_20 (Jr, ALUOp[1], not_2_out, not_3_out, not_4_out, Funct[3], not_6_out, not_7_out, not_8_out);
  or or_1 (Operation[0], and_17_out, and_18_out, and_19_out);
  or or_2 (Operation[2], and_1_out, and_2_out, and_3_out, and_4_out, and_5_out, and_6_out);
  or or_3 (Operation[1], and_7_out, and_8_out, and_9_out, and_10_out, and_11_out, and_12_out, and_13_out, and_14_out, and_15_out, and_16_out);
endmodule

module IBreakDown (
  input  [31:0] Instruction,
  output [5:0] Funct,
  output [4:0] Shamt,
  output [4:0] RD,
  output [4:0] RT,
  output [4:0] RS,
  output [5:0] OPCode,
  output [15:0] Inmediate,
  output [25:0] Address
);


  assign Address = Instruction[25:0];
  assign Funct = Instruction[5:0];
  assign Inmediate = Instruction[15:0];
  assign OPCode = Instruction[31:26];
  assign RD = Instruction[15:11];
  assign RS = Instruction[25:21];
  assign RT = Instruction[20:16];
  assign Shamt = Instruction[10:6];

  // Other names for the same wires on the sheet: ADDR[25:0] = Instruction[25:0]; INM[15:0] = Instruction[15:0]

  // Notes on the sheet:
  //   10 - 6
  //   15-11
  //   20-16
  //   25-21
  //   26-31
endmodule

module DataMemory (
  input  [31:0] Address,
  input  [31:0] WriteData,
  input  MemWrite,
  input  MemRead,
  input  CLK,
  input  [1:0] LoadType,
  output [31:0] ReadData
);

  wire [15:0] multiplexer_1_out;
  wire [31:0] bit_extender_1_out, ram_1_dout;

  RAM #(.addrWidth(24), .asyncread("true"), .dataWidth(32)) ram_1 (
    .addr(Address[25:2]), .we(MemWrite), .oe(MemRead), .clk(CLK), .din(WriteData), .dout(ram_1_dout));
  Multiplexer #(.select(2), .width(16)) multiplexer_1 (
    .in0(ram_1_dout[15:0]), .in2(ram_1_dout[31:16]), .out(multiplexer_1_out), .sel(Address[1:0]));  // open: in1, in3
  assign bit_extender_1_out = {{16{1'b0}}, multiplexer_1_out};  // Bit_Extender bit_extender_1
  Multiplexer #(.select(2), .width(32)) multiplexer_2 (
    .in0(ram_1_dout), .in1(bit_extender_1_out), .out(ReadData), .sel(LoadType));  // open: in2, in3
endmodule
